// Digital circuit ALU.dig as structural Verilog
module ALU (
  input  [3:0] Mode,
  input  [7:0] A,
  input  [7:0] B,
  input  Cin,
  output Cout,
  output Zero,
  output [7:0] Out
);

  wire add_1_c_o, sub_1_c_o;
  wire [7:0] add_1_s, and_1_out, barrelshifter_1_out, barrelshifter_2_out, div_1_q, div_1_r, or_1_out,
       sub_1_s, xor_1_out;
  wire [15:0] mul_1_mul;

  Add #(.Bits(8)) add_1 (.a(A), .b(B), .c_i(Cin), .s(add_1_s), .c_o(add_1_c_o));
  Sub #(.Bits(8)) sub_1 (.a(A), .b(B), .c_i(Cin), .s(sub_1_s), .c_o(sub_1_c_o));
  Mul #(.Bits(8)) mul_1 (.a(A), .b(B), .mul(mul_1_mul));
  Div #(.Bits(8)) div_1 (.a(A), .b(B), .q(div_1_q), .r(div_1_r));
  BarrelShifter #(.Bits(8)) barrelshifter_1 (.in(A), .shift(B[3:0]), .out(barrelshifter_1_out));
  BarrelShifter #(.Bits(8), .direction("right")) barrelshifter_2 (.in(A), .shift(B[3:0]), .out(barrelshifter_2_out));
  assign and_1_out = A & B;  // And and_1, 8 bits wide
  assign or_1_out = A | B;  // Or or_1, 8 bits wide
  assign xor_1_out = A ^ B;  // XOr xor_1, 8 bits wide
  Multiplexer #(.Selector_Bits(4)) multiplexer_1 (
    .sel(Mode), .in_0(Cin), .in_1(add_1_c_o), .in_2(sub_1_c_o), .in_3(Cin), .in_4(Cin), .in_5(Cin),
    .in_6(Cin), .in_7(Cin), .in_8(Cin), .in_9(Cin), .in_10(Cin), .in_11(Cin), .in_12(Cin), .in_13(Cin),
    .in_14(Cin), .in_15(Cin), .out(Cout));
  Multiplexer #(.Selector_Bits(4), .Bits(8)) multiplexer_2 (
    .sel(Mode), .in_0(A), .in_1(add_1_s), .in_2(sub_1_s), .in_3(mul_1_mul[7:0]), .in_4(div_1_q),
    .in_5(div_1_r), .in_6(barrelshifter_1_out), .in_7(barrelshifter_2_out), .in_8(and_1_out),
    .in_9(or_1_out), .in_10(xor_1_out), .in_11(8'hbd), .in_12(8'hbd), .in_13(8'hbd), .in_14(8'hbd),
    .in_15(8'hbd), .out(Out));
  nor nor_1 (Zero, Out[0], Out[1], Out[2], Out[3], Out[4], Out[5], Out[6], Out[7]);

  // Notes on the sheet:
  //   This whole mess of an ALU really needs to be remade properly at some point
endmodule
