// Digital circuit CPU.dig as structural Verilog
module CPU (
  input  Rise,
  input  Fall,
  input  [7:0] ROMIn,
  input  [7:0] MemIn,
  output [7:0] ROMAddr,
  output [7:0] MemAddr,
  output [7:0] MemOut,
  output MemWrite,
  output MemRead
);

  wire alu_1_cout, and_1_out, and_2_out, and_3_out, carry, clrCarry, comparator_1_eq, comparator_2_eq,
       control_1_nextfetchmode, destMemAddr, destRa, not_1_out, not_3_out, romMode, setImmed, setRegs;
  wire [0:0] control_1_pcmode, control_1_pcmode_2;
  wire [1:0] control_1_dest, control_1_srca, control_1_srcb;
  wire [3:0] Active_registers_q, control_1_alumode;
  wire [7:0] GPRs_da, GPRs_db, Immediate_value_q, multiplexer_1_out, multiplexer_2_out, multiplexer_3_out,
       pc, PC_Adder_s;

  Control control_1 (
    .Rise(Rise), .Instruction(ROMIn[7:4]), .NextFetchMode(control_1_nextfetchmode),
    .PCMode({control_1_pcmode_2[0], control_1_pcmode[0]}), .ALUMode(control_1_alumode),
    .SrcA(control_1_srca), .SrcB(control_1_srcb), .Dest(control_1_dest), .ROMMode(romMode),
    .ClrCarry(clrCarry));
  Register #(.Bits(4)) Active_registers (.D(ROMIn[3:0]), .C(Rise), .en(setRegs), .Q(Active_registers_q));
  Register #(.Bits(8)) Immediate_value (.D(ROMIn), .C(Rise), .en(setImmed), .Q(Immediate_value_q));
  // Probe rA # on Active_registers_q[3:2]
  // Probe Memory value on MemIn
  Decoder #(.Selector_Bits(2)) decoder_1 (
    .sel(control_1_dest), .out_1(destRa), .out_2(MemWrite), .out_3(destMemAddr));  // open: out_0
  // Probe rB # on Active_registers_q[1:0]
  // Probe SrcA on control_1_srca
  // Probe SrcB on control_1_srcb
  // Probe Dest on control_1_dest
  RegisterFile #(.Bits(8)) GPRs (
    .Din(MemOut), .we(destRa), .Rw(Active_registers_q[3:2]), .C(Fall), .Ra(Active_registers_q[3:2]),
    .Rb(Active_registers_q[1:0]), .Da(GPRs_da), .Db(GPRs_db));
  Register #(.Bits(8), .isProgramCounter("true")) u_PC (.D(multiplexer_3_out), .C(Fall), .en(1'b1), .Q(pc));
  // Probe rA on GPRs_da
  // Probe rB on GPRs_db
  Multiplexer #(.Selector_Bits(2), .Bits(8)) multiplexer_1 (
    .sel(control_1_srca), .in_0(GPRs_da), .in_1(GPRs_db), .in_2(Immediate_value_q), .in_3(MemIn),
    .out(multiplexer_1_out));
  Multiplexer #(.Selector_Bits(2), .Bits(8)) multiplexer_2 (
    .sel(control_1_srcb), .in_0(GPRs_da), .in_1(GPRs_db), .in_2(Immediate_value_q), .in_3(MemIn),
    .out(multiplexer_2_out));
  ALU alu_1 (
    .Mode(control_1_alumode), .A(multiplexer_1_out), .B(multiplexer_2_out), .Cin(carry), .Cout(alu_1_cout),
    .Out(MemOut));  // open: Zero
  Register nextFetchMode (.D(control_1_nextfetchmode), .C(Fall), .en(1'b1), .Q(setImmed));
  and and_1 (and_1_out, control_1_pcmode[0], carry);
  not not_1 (not_1_out, clrCarry);
  and and_2 (and_2_out, not_1_out, alu_1_cout);
  not not_2 (setRegs, setImmed);
  and and_3 (and_3_out, control_1_pcmode[0], not_3_out);
  not not_3 (not_3_out, control_1_pcmode_2[0]);
  Add #(.Bits(8)) PC_Adder (
    .a(pc), .b({{7{1'b0}}, control_1_pcmode_2[0]}), .c_i(and_1_out), .s(PC_Adder_s));  // open: c_o
  Register u_Carry (.D(and_2_out), .C(Fall), .en(1'b1), .Q(carry));
  Register #(.Bits(8)) Memory_address (.D(MemOut), .C(Fall), .en(destMemAddr), .Q(MemAddr));
  Multiplexer #(.Bits(8)) multiplexer_3 (.sel(and_3_out), .in_0(PC_Adder_s), .in_1(MemOut), .out(multiplexer_3_out));
  Comparator #(.Bits(2)) comparator_1 (.a(control_1_srca), .b(2'b11), .eq(comparator_1_eq));  // open: gt, lt
  Comparator #(.Bits(2)) comparator_2 (.a(control_1_srcb), .b(2'b11), .eq(comparator_2_eq));  // open: gt, lt
  Multiplexer #(.Bits(8)) multiplexer_4 (.sel(romMode), .in_0(pc), .in_1(MemAddr), .out(ROMAddr));
  or or_1 (MemRead, comparator_1_eq, comparator_2_eq);

  // Other names for the same wires on the sheet: destMem = MemWrite

  // Notes on the sheet:
  //   Rise > ready > fall
  //   Instruction decode
  //   Ready ASAP
  //   Data fetch
  //   Execute
  //   Fall > ready > next rise
  //   Fetch next instruction
  //   Write back
  //   <-- It's a miracle this mess even works
endmodule
