// Digital circuit FallingEdgeDetector.dig as structural Verilog
module FallingEdgeDetector (
  input  In,
  output Out
);

  wire delay_1_out, not_1_out;

  not not_1 (not_1_out, In);
  and and_1 (Out, not_1_out, delay_1_out);
  Delay #(.delayTime(5)) delay_1 (.in(In), .out(delay_1_out));
endmodule
