// Digital circuit Main.dig as structural Verilog
module Main (
  input  Clock,
  input  Enable_clock
);

  wire allowclock, and_1_out, and_2_out, and_3_out, and_4_out, and_5_out, busread, buswrite, delay_1_out,
       demultiplexer_1_out_1, demultiplexer_1_out_2, demultiplexer_1_out_3, demultiplexer_1_out_4,
       demultiplexer_1_out_5, demultiplexer_1_out_6, demultiplexer_1_out_7, demultiplexer_2_out_6,
       dipswitch_1_out, fall, Manual_pulse_out, or_1_out, or_2_out, ram, rise, rs_ff_as_1_q, telnet_1_av;
  wire [3:0] Memory_lookup_thing_d;
  wire [7:0] busaddr, busin, busout, ColorHigh_q, ColorLow_q, cpu_1_romaddr, rom_1_d, X_q, Y_q;

  CPU cpu_1 (
    .Rise(rise), .Fall(fall), .ROMIn(rom_1_d), .MemIn(busin), .ROMAddr(cpu_1_romaddr), .MemAddr(busaddr),
    .MemOut(busout), .MemWrite(buswrite), .MemRead(busread));
  Button Manual_pulse (.out(Manual_pulse_out));
  and and_1 (and_1_out, Enable_clock, allowclock, Clock);
  or or_1 (or_1_out, Manual_pulse_out, and_1_out);
  and and_2 (and_2_out, buswrite, ram);
  and and_3 (and_3_out, busread, ram);
  RisingEdgeDetector risingedgedetector_1 (.In(or_1_out), .Out(rise));
  FallingEdgeDetector fallingedgedetector_1 (.In(or_1_out), .Out(fall));
  // Probe Cycle on or_1_out
  ROM #(.AddrBits(8), .Bits(8)) rom_1 (.A(cpu_1_romaddr), .sel(1'b1), .D(rom_1_d));
  RAMDualPort #(.AddrBits(8), .Bits(8)) ramdualport_1 (
    .A(busaddr), .Din(busout), .str(and_2_out), .C(fall), .ld(and_3_out), .D(busin));
  ROM #(.AddrBits(8), .Bits(4)) Memory_lookup_thing (.A(busaddr), .sel(1'b1), .D(Memory_lookup_thing_d));
  and and_4 (and_4_out, Memory_lookup_thing_d[3], buswrite);
  Terminal terminal_1 (.D(busout), .C(fall), .en(demultiplexer_1_out_7));
  Demultiplexer #(.Selector_Bits(3)) demultiplexer_1 (
    .sel(Memory_lookup_thing_d[2:0]), .in(and_4_out), .out_1(demultiplexer_1_out_1),
    .out_2(demultiplexer_1_out_2), .out_3(demultiplexer_1_out_3), .out_4(demultiplexer_1_out_4),
    .out_5(demultiplexer_1_out_5), .out_6(demultiplexer_1_out_6), .out_7(demultiplexer_1_out_7));  // open: out_0
  not not_1 (ram, Memory_lookup_thing_d[3]);
  and and_5 (and_5_out, busread, Memory_lookup_thing_d[3]);
  Demultiplexer #(.Selector_Bits(3)) demultiplexer_2 (
    .sel(Memory_lookup_thing_d[2:0]), .in(and_5_out), .out_6(demultiplexer_2_out_6));  // open: out_0, out_1, out_2, out_3, out_4, out_5, out_7
  Telnet #(.telnetEscape("false"), .port(5761)) telnet_1 (
    .in(busout), .C(fall), .wr(demultiplexer_1_out_6), .rd(demultiplexer_2_out_6), .out(busin),
    .av(telnet_1_av));
  LED Data (.in(telnet_1_av));
  Register #(.Bits(8)) ColorLow (.D(busout), .C(fall), .en(demultiplexer_1_out_5), .Q(ColorLow_q));
  Register #(.Bits(8)) ColorHigh (.D(busout), .C(fall), .en(demultiplexer_1_out_4), .Q(ColorHigh_q));
  Register #(.Bits(8)) X (.D(busout), .C(fall), .en(demultiplexer_1_out_3), .Q(X_q));
  Register #(.Bits(8)) Y (.D(busout), .C(fall), .en(demultiplexer_1_out_2), .Q(Y_q));
  or or_2 (or_2_out, demultiplexer_1_out_2, demultiplexer_1_out_3, demultiplexer_1_out_4, demultiplexer_1_out_5);
  RS_FF_AS rs_ff_as_1 (.S(demultiplexer_1_out_1), .R(rise), .Q(rs_ff_as_1_q), .nQ(allowclock));
  Delay #(.delayTime(5)) delay_1 (.in(fall), .out(delay_1_out));
  LED Break (.in(rs_ff_as_1_q));
  GraphicCard #(.graphicHeight(256), .graphicWidth(256), .Bits(16)) graphiccard_1 (
    .A({1'b0, Y_q, X_q}), .str(or_2_out), .C(delay_1_out), .ld(1'b0), .B(dipswitch_1_out),
    .D({ColorHigh_q, ColorLow_q}));
  DipSwitch dipswitch_1 (.out(dipswitch_1_out));

  // Notes on the sheet:
  //   Clock: Hz: 50000
  //   Clock
  //   CPU & ROM, RAM
  //   contents of rom_1 (hex, n*v repeats v):
  //   10,1,18,fe,4b,26,2e,53,fd,2e,53,fc,74,51,fb,1c,6,f0,dc,2c,7c,53
  //   ,fa,43,18,2,f0,d8,50,f9
  //   Peripherals
  //   contents of Memory_lookup_thing (hex, n*v repeats v):
  //   249*0,f9,a,b,c,d,e,f
  //   Terminal
  //   Telnet / "Serial"
  //   Display
  //   Breakpoint thing
endmodule
